// Logisim project 01-XOR Gate.circ as structural Verilog: 1 circuit, main circuit main
module main (
  input  in_1,
  output out_2
);

  wire and_1_out, and_2_out, clock_1_out, not_1_out, not_2_out;

  Clock clock_1 (.out(clock_1_out));
  not not_1 (not_1_out, clock_1_out);
  not not_2 (not_2_out, in_1);
  and and_1 (and_1_out, not_1_out, in_1);
  and and_2 (and_2_out, clock_1_out, not_2_out);
  or or_1 (out_2, and_1_out, and_2_out);
endmodule
