// Logisim project 05-Selector41_4bits.circ as structural Verilog: 1 circuit, main circuit main
module main (
  input  in_1,
  input  in_2,
  input  [3:0] in_3,
  input  [3:0] in_4,
  input  [3:0] in_5,
  input  [3:0] in_6,
  output [3:0] out_7
);

  wire [3:0] and_1_out, and_2_out, and_3_out, and_4_out, not_1_out, not_2_out;

  assign not_1_out = ~{4{in_1}};  // NOT_Gate not_1, 4 bits wide
  assign not_2_out = ~{4{in_2}};  // NOT_Gate not_2, 4 bits wide
  assign and_1_out = in_3 & not_2_out & not_1_out;  // AND_Gate and_1, 4 bits wide
  assign and_2_out = in_4 & not_2_out & {4{in_1}};  // AND_Gate and_2, 4 bits wide
  assign and_3_out = in_5 & {4{in_2}} & not_1_out;  // AND_Gate and_3, 4 bits wide
  assign and_4_out = in_6 & {4{in_2}} & {4{in_1}};  // AND_Gate and_4, 4 bits wide
  assign out_7 = and_1_out | and_2_out | and_3_out | and_4_out;  // OR_Gate or_1, 4 bits wide
endmodule
