// Logisim project 07-Encoder83.circ as structural Verilog: 1 circuit, main circuit main
module main (
  input  in_1,
  input  in_2,
  input  in_3,
  input  in_4,
  input  in_5,
  input  in_6,
  input  in_7,
  input  in_8,
  input  in_9,
  input  in_10,
  input  in_11,
  input  in_12,
  input  in_13
);

  wire or_1_out, or_2_out, or_3_out, or_4_out;

  or or_1 (or_1_out, in_1, in_4, in_7, in_10, in_13);
  or or_2 (or_2_out, in_4, in_3, in_9, in_10);
  or or_3 (or_3_out, in_6, in_7, in_9, in_10);
  or or_4 (or_4_out, in_11, in_13);
endmodule
