// Logisim project 09-Selector21.circ as structural Verilog: 2 circuits, main circuit main
module main (
  input  C,
  input  ENB,
  input  S1,
  input  S2,
  output D
);

  wire and_1_out, and_2_out, not_1_out;

  not not_1 (not_1_out, C);
  and and_1 (and_1_out, S1, ENB, not_1_out);
  and and_2 (and_2_out, S2, ENB, C);
  or or_1 (D, and_1_out, and_2_out);
endmodule

module _1 (
  input  in_1,
  input  in_2,
  input  in_3,
  input  in_4,
  input  in_5,
  input  in_6
);

  wire main_1_d, undriven;

  // NOT_Gate not_1 is placed but not wired
  // NOT_Gate not_2 is placed but not wired
  main main_1 (.C(undriven), .S1(in_1), .S2(in_3), .D(main_1_d));  // open: ENB
  main main_2 (.S1(in_2), .S2(main_1_d));  // open: C, ENB, D
endmodule
