// Logisim project 10-Gray To BCD.circ as structural Verilog: 1 circuit, main circuit main
module main (
  input  in_1,
  input  in_2,
  input  EN,
  input  A,
  input  B,
  input  C,
  input  in_7,
  input  D,
  output W,
  output X,
  output Y,
  output Z
);

  wire nand_1_out, nand_2_out, nand_3_out, nand_4_out, nand_5_out, nand_6_out, nand_7_out, nand_8_out;

  nand nand_1 (nand_1_out, C, C);
  nand nand_2 (nand_2_out, D, D);
  nand nand_3 (nand_3_out, nand_1_out, D);
  nand nand_4 (nand_4_out, C, nand_2_out);
  nand nand_5 (nand_5_out, nand_1_out, nand_2_out);
  nand nand_6 (nand_6_out, C, D);
  Multiplexer #(.select(2)) multiplexer_1 (
    .in0(in_2), .in1(in_2), .in2(in_2), .in3(in_1), .out(W), .sel({A, B}), .en(EN));
  Multiplexer #(.select(2)) multiplexer_2 (
    .in0(in_2), .in1(in_1), .in2(in_2), .in3(in_2), .out(X), .sel({A, B}), .en(EN));
  nand nand_7 (nand_7_out, nand_3_out, nand_4_out);
  nand nand_8 (nand_8_out, nand_5_out, nand_6_out);
  Multiplexer #(.select(2)) multiplexer_3 (
    .in0(C), .in1(nand_1_out), .in2(in_7), .in3(in_7), .out(Y), .sel({A, B}), .en(EN));
  Multiplexer #(.select(2)) multiplexer_4 (
    .in0(nand_7_out), .in1(nand_8_out), .in2(in_7), .in3(D), .out(Z), .sel({A, B}), .en(EN));
endmodule
