// Logisim project 12-BloodCheck.circ as structural Verilog: 1 circuit, main circuit main
module main (
  input  X0,
  input  X1,
  input  Y0,
  input  Y1
);

  wire and_1_out, and_2_out, and_3_out, and_4_out, and_5_out, and_6_out, and_7_out, and_8_out, and_9_out,
       not_1_out, not_2_out, not_3_out, not_4_out, not_5_out, not_6_out, not_7_out, not_8_out, not_9_out,
       not_10_out, not_11_out, not_12_out, not_13_out, not_14_out, not_15_out, not_16_out, not_17_out,
       not_18_out, or_1_out;

  not not_1 (not_1_out, X0);
  not not_2 (not_2_out, X1);
  not not_3 (not_3_out, Y0);
  not not_4 (not_4_out, Y1);
  not not_5 (not_5_out, X0);
  not not_6 (not_6_out, X1);
  not not_7 (not_7_out, Y1);
  not not_8 (not_8_out, X0);
  not not_9 (not_9_out, Y0);
  not not_10 (not_10_out, X0);
  not not_11 (not_11_out, Y1);
  not not_12 (not_12_out, X1);
  not not_13 (not_13_out, Y1);
  not not_14 (not_14_out, Y0);
  not not_15 (not_15_out, Y1);
  not not_16 (not_16_out, Y0);
  not not_17 (not_17_out, Y1);
  and and_1 (and_1_out, not_1_out, not_2_out, not_3_out, not_4_out);
  and and_2 (and_2_out, not_5_out, not_6_out, Y0, not_7_out);
  and and_3 (and_3_out, not_8_out, X1, not_9_out, Y1);
  and and_4 (and_4_out, not_10_out, X1, Y0, not_11_out);
  and and_5 (and_5_out, X0, not_12_out, Y0, not_13_out);
  and and_6 (and_6_out, X0, X1, not_14_out, not_15_out);
  and and_7 (and_7_out, X0, X1, not_16_out, Y1);
  and and_8 (and_8_out, X0, X1, Y0, not_17_out);
  and and_9 (and_9_out, X0, X1, Y0, Y1);
  or or_1 (or_1_out, and_1_out, and_2_out, and_3_out, and_4_out, and_5_out, and_6_out, and_7_out, and_8_out, and_9_out);
  LED led_1 (.in(or_1_out));
  LED led_2 (.in(not_18_out));
  not not_18 (not_18_out, or_1_out);
endmodule
