// Logisim project 13-JK Trigger.circ as structural Verilog: 1 circuit, main circuit main
module main (
  input  in_1,
  input  in_2,
  input  in_3
);

  wire nand_1_out, nand_2_out, or_1_out, or_2_out;

  nand nand_1 (nand_1_out, in_1, or_2_out, in_2);
  nand nand_2 (nand_2_out, in_2, or_1_out, in_3);
  or or_1 (or_1_out, ~nand_1_out, ~or_2_out);  // OR_Gate
  or or_2 (or_2_out, ~or_1_out, ~nand_2_out);  // OR_Gate
endmodule
