// Logisim project 16-Control.circ as structural Verilog: 1 circuit, main circuit main
// A
module main (
  input  RST,
  input  [3:0] DATA,
  input  EN,
  input  RST_2,
  input  EN_2,
  input  [3:0] DATA_2,
  output out_7,
  output out_8
);

  wire A_2_q, A_2_qn, A_q, A_qn, ADD, adder_1_cout, and_1_out, and_2_out, and_3_out, and_4_out, and_5_out,
       B_2_q, B_2_qn, B_q, B_qn, CAP, clock_1_out, clock_2_out, CLR, LDA, LDB, LDC, LDRA, LDRB, not_1_out,
       or_1_out, or_2_out, or_3_out, or_4_out, or_5_out, xor_1_out;
  wire [3:0] adder_1_out, controlled_buffer_1_out, controlled_buffer_2_out, controlled_buffer_3_out, RA_q,
       RB_q, register_1_q, register_2_q;

  Clock clock_1 (.out(clock_1_out));
  Clock clock_2 (.out(clock_2_out));
  or or_1 (or_1_out, and_1_out, A_2_q);
  not not_1 (not_1_out, clock_1_out);
  D_Flip_Flop A (.clk(clock_1_out), .D(or_3_out), .Q(A_q), .Qn(A_qn), .en(EN), .reset(RST));  // open: preset
  D_Flip_Flop B (.clk(clock_1_out), .D(or_2_out), .Q(B_q), .Qn(B_qn), .en(EN), .reset(RST));  // open: preset
  or or_2 (or_2_out, A_q, B_q);
  or or_3 (or_3_out, A_qn, B_qn);
  D_Flip_Flop A_2 (.clk(clock_2_out), .D(or_4_out), .Q(A_2_q), .Qn(A_2_qn), .en(EN_2), .reset(RST_2));  // open: preset
  D_Flip_Flop B_2 (.clk(clock_2_out), .D(or_1_out), .Q(B_2_q), .Qn(B_2_qn), .en(EN_2), .reset(RST_2));  // open: preset
  or or_4 (or_4_out, A_2_qn, B_2_qn);
  and and_1 (and_1_out, B_2_q, out_8);
  and and_2 (and_2_out, B_qn, A_qn);
  and and_3 (and_3_out, A_q, B_q);
  and and_4 (and_4_out, A_q, B_q);
  and and_5 (and_5_out, A_qn, B_q);
  or or_5 (or_5_out, and_2_out, and_3_out);
  xor xor_1 (xor_1_out, A_q, B_q);
  or or_6 (ADD, and_4_out, and_5_out);
  and and_6 (CAP, B_2_q, A_2_qn);
  and and_7 (LDRA, B_2_qn, A_2_q);
  xnor xnor_1 (LDRB, A_2_q, B_2_q);
  // AND_Gate and_8 is placed but not wired
  // XOR_Gate xor_2 is placed but not wired
  and u_LDA (LDA, or_5_out, not_1_out);
  and u_LDB (LDB, xor_1_out, not_1_out);
  and u_LDC (LDC, B_q, A_qn, not_1_out);
  and u_CLR (CLR, B_qn, A_qn);
  // OR_Gate or_7 is placed but not wired
  Register #(.width(4)) register_1 (.D(DATA), .en(EN), .Q(register_1_q), .clk(LDA), .clr(RST));
  Register #(.width(4)) register_2 (.D(adder_1_out), .en(EN), .Q(register_2_q), .clk(LDB), .clr(RST));
  Register #(.width(4)) RA (.D(RB_q), .Q(RA_q), .clk(LDRA));  // open: en, clr
  Register #(.width(4)) RB (.D(DATA_2), .Q(RB_q), .clk(LDRB));  // open: en, clr
  assign controlled_buffer_1_out = ADD ? register_2_q : 4'bz;  // Controlled_Buffer controlled_buffer_1
  assign controlled_buffer_2_out = CAP ? RA_q : 4'bz;  // Controlled_Buffer controlled_buffer_2
  assign controlled_buffer_3_out = CAP ? RB_q : 4'bz;  // Controlled_Buffer controlled_buffer_3
  Adder #(.width(4)) adder_1 (
    .a(register_1_q), .b(controlled_buffer_1_out), .out(adder_1_out), .cout(adder_1_cout));  // open: cin
  Comparator #(.width(4)) comparator_1 (
    .a(controlled_buffer_2_out), .b(controlled_buffer_3_out), .gt(out_8));  // open: eq, lt
  Register #(.width(1)) register_3 (.D(adder_1_cout), .en(EN), .Q(out_7), .clk(LDC), .clr(CLR));

  // Other names for the same wires on the sheet: Z = out_8
endmodule
