// Logisim project 17-ControlUpgraded.circ as structural Verilog: 1 circuit, main circuit main
// twosComplement
module main (
  input  RST,
  input  [3:0] DATA,
  input  EN,
  input  RST_2,
  input  EN_2,
  input  [3:0] DATA_2,
  input  RST_3,
  input  [3:0] DATA_3,
  input  EN_3,
  input  RST_4,
  input  EN_4,
  input  [3:0] DATA_4,
  input  RST_5,
  input  EN_5,
  input  [3:0] DATA_5,
  input  RST_6,
  input  [3:0] DATA_6,
  input  EN_6,
  output out_19,
  output out_20,
  output out_21,
  output out_22,
  output out_23,
  output out_24
);

  wire A_2_qn, A_3_q, A_3_qn, A_4_qn, A_5_qn, A_6_q, A_6_qn, A_qn, ADD, ADD2, ADD3, adder_1_cout,
       adder_2_cout, adder_3_cout, and_1_out, and_2_out, and_3_out, and_4_out, and_5_out, and_6_out,
       and_7_out, and_8_out, and_9_out, and_10_out, B_2_qn, B_3_q, B_3_qn, B_4_q, B_4_qn, B_5_q, B_5_qn,
       B_6_q, B_6_qn, B_qn, C_2_q, C_2_qn, C_q, C_qn, CAP, CAP2, CAP3, clock_1_out, clock_2_out, clock_3_out,
       clock_4_out, clock_5_out, clock_6_out, CLR, CLR2, CLR3, D_qn, LDA, LDA2, LDA3, LDB, LDB2, LDB3, LDC,
       LDC2, LDC3, LDRA, LDRA2, LDRA3, LDRB, LDRB2, LDRB3, multiplexer_1_out, multiplexer_2_out,
       multiplexer_3_out, multiplexer_4_out, not_1_out, not_2_out, not_3_out, not_4_out, not_5_out, or_1_out,
       or_2_out, or_3_out, or_4_out, or_5_out, or_6_out, or_7_out, or_8_out, or_9_out, or_10_out, xor_1_out,
       xor_2_out;
  wire [1:0] A_2_q;
  wire [1:1] B_q;
  wire [3:0] adder_1_out, adder_2_out, adder_3_out, controlled_buffer_1_out, controlled_buffer_2_out,
       controlled_buffer_3_out, controlled_buffer_4_out, controlled_buffer_5_out, controlled_buffer_6_out,
       controlled_buffer_7_out, controlled_buffer_8_out, controlled_buffer_9_out, RA_2_q, RA_3_q, RA_q,
       RB_2_q, RB_3_q, RB_q, register_1_q, register_2_q, register_3_q, register_4_q, register_5_q,
       register_6_q;

  Clock clock_1 (.out(clock_1_out));
  Clock clock_2 (.out(clock_2_out));
  Clock clock_3 (.out(clock_3_out));
  Clock clock_4 (.out(clock_4_out));
  Clock clock_5 (.out(clock_5_out));
  Clock clock_6 (.out(clock_6_out));
  not not_1 (not_1_out, clock_5_out);
  or or_1 (or_1_out, A_3_q, and_4_out);
  or or_2 (or_2_out, and_5_out, B_3_q);
  and and_1 (and_1_out, ADD, B_5_qn);
  or or_3 (or_3_out, ADD, B_5_qn);
  or or_4 (or_4_out, A_6_qn, B_6_qn);
  and and_2 (and_2_out, B_6_q, out_20);
  or or_5 (or_5_out, and_2_out, A_6_q);
  D_Flip_Flop A (
    .clk(clock_3_out), .D(multiplexer_2_out), .Q(ADD2), .Qn(A_qn), .en(EN_3), .reset(RST_3));  // open: preset
  D_Flip_Flop B (
    .clk(clock_3_out), .D(multiplexer_1_out), .Q(B_q[1]), .Qn(B_qn), .en(EN_3), .reset(RST_3));  // open: preset
  Multiplexer #(.select(2)) multiplexer_1 (
    .in0(1'b0), .in1(1'b1), .in2(1'b0), .in3(1'b0), .out(multiplexer_1_out), .sel({B_q[1], ADD2}), .en(EN_3));
  Multiplexer #(.select(2)) multiplexer_2 (
    .in0(1'b1), .in1(1'b1), .in2(1'b0), .in3(1'b1), .out(multiplexer_2_out), .sel({B_q[1], ADD2}), .en(EN_3));
  D_Flip_Flop A_2 (
    .clk(clock_4_out), .D(multiplexer_3_out), .Q(A_2_q[0]), .Qn(A_2_qn), .en(EN_4), .reset(RST_4));  // open: preset
  D_Flip_Flop B_2 (
    .clk(clock_4_out), .D(multiplexer_4_out), .Q(A_2_q[1]), .Qn(B_2_qn), .en(EN_4), .reset(RST_4));  // open: preset
  Multiplexer #(.select(2)) multiplexer_3 (
    .in0(1'b1), .in1(1'b1), .in2(1'b1), .in3(1'b0), .out(multiplexer_3_out), .sel(A_2_q), .en(EN_4));
  Multiplexer #(.select(2)) multiplexer_4 (
    .in0(1'b0), .in1(1'b1), .in2(out_22), .in3(1'b1), .out(multiplexer_4_out), .sel(A_2_q), .en(EN_4));
  D_Flip_Flop A_3 (.clk(clock_5_out), .D(and_3_out), .Q(A_3_q), .Qn(A_3_qn), .en(EN_5), .reset(RST_5));  // open: preset
  D_Flip_Flop B_3 (.clk(clock_5_out), .D(or_1_out), .Q(B_3_q), .Qn(B_3_qn), .en(EN_5), .reset(RST_5));  // open: preset
  D_Flip_Flop C (.clk(clock_5_out), .D(or_2_out), .Q(C_q), .Qn(C_qn), .en(EN_5), .reset(RST_5));  // open: preset
  D_Flip_Flop D (.clk(clock_5_out), .D(C_q), .Q(CAP3), .Qn(D_qn), .en(EN_5), .reset(RST_5));  // open: preset
  and and_3 (and_3_out, A_3_qn, B_3_qn, C_qn, D_qn);
  and and_4 (and_4_out, not_5_out, CAP3);
  and and_5 (and_5_out, out_23, CAP3);
  D_Flip_Flop A_4 (.clk(clock_6_out), .D(and_6_out), .Q(CLR3), .Qn(A_4_qn), .en(EN_6), .reset(RST_6));  // open: preset
  D_Flip_Flop B_4 (.clk(clock_6_out), .D(or_6_out), .Q(B_4_q), .Qn(B_4_qn), .en(EN_6), .reset(RST_6));  // open: preset
  D_Flip_Flop C_2 (.clk(clock_6_out), .D(B_4_q), .Q(C_2_q), .Qn(C_2_qn), .en(EN_6), .reset(RST_6));  // open: preset
  or or_6 (or_6_out, CLR3, C_2_q);
  and and_6 (and_6_out, A_4_qn, B_4_qn, C_2_qn);
  D_Flip_Flop A_5 (.clk(clock_1_out), .D(or_3_out), .Q(ADD), .Qn(A_5_qn), .en(EN), .reset(RST));  // open: preset
  D_Flip_Flop B_5 (.clk(clock_1_out), .D(and_1_out), .Q(B_5_q), .Qn(B_5_qn), .en(EN), .reset(RST));  // open: preset
  D_Flip_Flop A_6 (.clk(clock_2_out), .D(or_4_out), .Q(A_6_q), .Qn(A_6_qn), .en(EN_2), .reset(RST_2));  // open: preset
  D_Flip_Flop B_6 (.clk(clock_2_out), .D(or_5_out), .Q(B_6_q), .Qn(B_6_qn), .en(EN_2), .reset(RST_2));  // open: preset
  not not_2 (not_2_out, clock_1_out);
  not not_3 (not_3_out, clock_3_out);
  and and_7 (and_7_out, B_qn, A_qn);
  and and_8 (and_8_out, ADD2, B_q[1]);
  not not_4 (not_4_out, clock_6_out);
  and and_9 (and_9_out, B_5_qn, A_5_qn);
  or or_7 (or_7_out, and_9_out, and_10_out);
  and and_10 (and_10_out, ADD, B_5_q);
  xor xor_1 (xor_1_out, ADD, B_5_q);
  and and_11 (CAP, B_6_q, A_6_qn);
  and and_12 (LDRA, B_6_qn, A_6_q);
  xnor xnor_1 (LDRB, A_6_q, B_6_q);
  or or_8 (or_8_out, and_7_out, and_8_out);
  xor xor_2 (xor_2_out, ADD2, B_q[1]);
  and and_13 (CAP2, A_2_q[1], A_2_qn);
  and and_14 (LDRA2, B_2_qn, A_2_q[0]);
  xnor xnor_2 (LDRB2, A_2_q[0], A_2_q[1]);
  or or_9 (or_9_out, A_3_q, C_q);
  not not_5 (not_5_out, out_23);
  or or_10 (or_10_out, CLR3, C_2_q);
  // AND_Gate and_15 is placed but not wired
  // XOR_Gate xor_3 is placed but not wired
  and u_LDA (LDA, or_7_out, not_2_out);
  and u_LDB (LDB, xor_1_out, not_2_out);
  and u_LDC (LDC, B_5_q, A_5_qn, not_2_out);
  and u_CLR (CLR, B_5_qn, A_5_qn);
  // XOR_Gate xor_4 is placed but not wired
  // AND_Gate and_16 is placed but not wired
  and LDA_2 (LDA2, or_8_out, not_3_out);
  and LDB_2 (LDB2, xor_2_out, not_3_out);
  and LDC_2 (LDC2, B_q[1], A_qn, not_3_out);
  and CLR_2 (CLR2, B_qn, A_qn);
  and and_17 (LDRA3, B_3_q, not_1_out);
  and and_18 (LDRB3, not_1_out, or_9_out);
  and LDA_3 (LDA3, or_10_out, not_4_out);
  and LDB_3 (LDB3, B_4_q, not_4_out);
  and LDC_3 (LDC3, B_4_q, not_4_out);
  or or_11 (ADD3, C_2_q, B_4_q);
  // OR_Gate or_12 is placed but not wired
  // OR_Gate or_13 is placed but not wired
  Register #(.width(4)) register_1 (.D(DATA), .en(EN), .Q(register_1_q), .clk(LDA), .clr(RST));
  Register #(.width(4)) register_2 (.D(adder_1_out), .en(EN), .Q(register_2_q), .clk(LDB), .clr(RST));
  Register #(.width(4)) RA (.D(RB_q), .Q(RA_q), .clk(LDRA), .clr(RST_2));  // open: en
  Register #(.width(4)) RB (.D(DATA_2), .Q(RB_q), .clk(LDRB), .clr(RST_2));  // open: en
  Register #(.width(4)) register_3 (.D(DATA_3), .en(EN_3), .Q(register_3_q), .clk(LDA2), .clr(RST_3));
  Register #(.width(4)) register_4 (.D(adder_2_out), .en(EN_3), .Q(register_4_q), .clk(LDB2), .clr(RST_3));
  Register #(.width(4)) RA_2 (.D(RB_2_q), .Q(RA_2_q), .clk(LDRA2), .clr(RST_4));  // open: en
  Register #(.width(4)) RB_2 (.D(DATA_4), .Q(RB_2_q), .clk(LDRB2), .clr(RST_4));  // open: en
  Register #(.width(4)) RA_3 (.D(RB_3_q), .Q(RA_3_q), .clk(LDRA3), .clr(RST_5));  // open: en
  Register #(.width(4)) RB_3 (.D(DATA_5), .Q(RB_3_q), .clk(LDRB3), .clr(RST_5));  // open: en
  Register #(.width(4)) register_5 (.D(DATA_6), .en(EN_6), .Q(register_5_q), .clk(LDA3), .clr(RST_6));
  Register #(.width(4)) register_6 (.D(adder_3_out), .en(EN_6), .Q(register_6_q), .clk(LDB3), .clr(RST_6));
  assign controlled_buffer_1_out = ADD ? register_2_q : 4'bz;  // Controlled_Buffer controlled_buffer_1
  assign controlled_buffer_2_out = CAP ? RA_q : 4'bz;  // Controlled_Buffer controlled_buffer_2
  assign controlled_buffer_3_out = CAP ? RB_q : 4'bz;  // Controlled_Buffer controlled_buffer_3
  assign controlled_buffer_4_out = ADD2 ? register_4_q : 4'bz;  // Controlled_Buffer controlled_buffer_4
  assign controlled_buffer_5_out = CAP2 ? RA_2_q : 4'bz;  // Controlled_Buffer controlled_buffer_5
  assign controlled_buffer_6_out = CAP2 ? RB_2_q : 4'bz;  // Controlled_Buffer controlled_buffer_6
  assign controlled_buffer_7_out = CAP3 ? RA_3_q : 4'bz;  // Controlled_Buffer controlled_buffer_7
  assign controlled_buffer_8_out = CAP3 ? RB_3_q : 4'bz;  // Controlled_Buffer controlled_buffer_8
  assign controlled_buffer_9_out = ADD3 ? register_6_q : 4'bz;  // Controlled_Buffer controlled_buffer_9
  Adder #(.width(4)) adder_1 (
    .a(register_1_q), .b(controlled_buffer_1_out), .out(adder_1_out), .cout(adder_1_cout));  // open: cin
  Comparator #(.width(4)) comparator_1 (
    .a(controlled_buffer_2_out), .b(controlled_buffer_3_out), .gt(out_20));  // open: eq, lt
  Adder #(.width(4)) adder_2 (
    .a(register_3_q), .b(controlled_buffer_4_out), .out(adder_2_out), .cout(adder_2_cout));  // open: cin
  Comparator #(.width(4)) comparator_2 (
    .a(controlled_buffer_5_out), .b(controlled_buffer_6_out), .gt(out_22));  // open: eq, lt
  Comparator #(.width(4)) comparator_3 (
    .a(controlled_buffer_7_out), .b(controlled_buffer_8_out), .gt(out_23));  // open: eq, lt
  Adder #(.width(4)) adder_3 (
    .a(register_5_q), .b(controlled_buffer_9_out), .out(adder_3_out), .cout(adder_3_cout));  // open: cin
  Register #(.width(1)) register_7 (.D(adder_1_cout), .en(EN), .Q(out_19), .clk(LDC), .clr(CLR));
  Register #(.width(1)) register_8 (.D(adder_2_cout), .en(EN_3), .Q(out_21), .clk(LDC2), .clr(CLR2));
  Register #(.width(1)) register_9 (.D(adder_3_cout), .en(EN_6), .Q(out_24), .clk(LDC3), .clr(CLR3));

  // Other names for the same wires on the sheet: EN2 = EN_3; EN3 = EN_6; Z = out_20; Z2 = out_22; Z3 = out_23

  // Notes on the sheet:
  //   加法控制器（计数器型）
  //   比较控制器（计数器型）
  //   加法控制器（选择器型）
  //   比较控制器（选择器型）
  //   MUXA
  //   MUXB
  //   比较控制器（定序型）
  //   加法控制器（定序型）
endmodule
