// Logisim project 02-Base Gate.circ as structural Verilog: 1 circuit, main circuit main
module main (
  input  in_1,
  input  in_2,
  output out_3,
  output out_4,
  output out_5
);

  and and_1 (out_3, in_1, in_2);
  or or_1 (out_4, in_1, in_2);
  not not_1 (out_5, in_1);
endmodule
